// Logisim project Logisim_Circuit.circ as structural Verilog: 1 circuit, main circuit Redesigned ALU
module Redesigned_ALU (
  input  CS0,
  input  CS1,
  input  CS2,
  input  B0,
  input  B1,
  input  B2,
  input  B3,
  input  A0,
  input  A1,
  input  A2,
  input  A3
);

  wire n7404_1__2__1y, n7404_1__4__2y, n7404_1__6__3y, n7404_1__8__4y, n7404_1__10__5y, n7404_1__12__6y,
       n7404_2__2__1y, n7404_2__4__2y, n7404_2__6__3y, n7404_2__8__4y, n7404_2__10__5y, n7404_2__12__6y,
       n7408_1__3__1y, n7408_1__6__2y, n7408_1__8__3y, n7408_1__11__4y, n7408_2__3__1y, n7408_2__6__2y,
       n7408_2__8__3y, n7408_2__11__4y, n7432_1__3__1y, n7432_1__6__2y, n7432_1__8__3y, n7432_1__11__4y,
       n7432_2__3__1y, n7432_2__6__2y, n7432_2__8__3y, n7432_2__11__4y, n7483_1__2__s3, n7483_1__6__s2,
       n7483_1__9__s1, n7483_1__14__cout, n7483_1__15__s4, n7486_1__3__1y, n7486_1__6__2y, n7486_1__11__4y,
       n74157_1__4__y1, n74157_1__7__y2, n74157_1__9__y3, n74157_1__12__y4, n74157_2__4__y1, n74157_2__7__y2,
       n74157_2__9__y3, n74157_2__12__y4, n74157_3__4__y1, n74157_3__7__y2, n74157_3__9__y3, n74157_3__12__y4;

  _7404 u_7404_1 (
    ._1__1A(B0), ._2__1Y(n7404_1__2__1y), ._3__2A(B1), ._4__2Y(n7404_1__4__2y), ._5__3A(B2),
    ._6__3Y(n7404_1__6__3y), ._7__GND(1'b0), ._14__Vcc(1'b1), ._13__6A(CS1), ._12__6Y(n7404_1__12__6y),
    ._11__5A(CS0), ._10__5Y(n7404_1__10__5y), ._9__4A(B3), ._8__4Y(n7404_1__8__4y));
  _74157 u_74157_1 (
    ._1__S(n7432_1__3__1y), ._2__A1(B0), ._3__B1(n7404_1__2__1y), ._4__Y1(n74157_1__4__y1), ._5__A2(B1),
    ._6__B2(n7404_1__4__2y), ._7__Y2(n74157_1__7__y2), ._8__GND(1'b0), ._16__Vcc(1'b1),
    ._15__G(n7408_2__8__3y), ._14__A4(B3), ._13__B4(n7404_1__8__4y), ._12__Y4(n74157_1__12__y4),
    ._11__A3(B2), ._10__B3(n7404_1__6__3y), ._9__Y3(n74157_1__9__y3));
  _74157 u_74157_2 (
    ._1__S(n7408_2__8__3y), ._2__A1(A0), ._3__B1(n7408_2__3__1y), ._4__Y1(n74157_2__4__y1), ._5__A2(A1),
    ._6__B2(n7408_2__6__2y), ._7__Y2(n74157_2__7__y2), ._8__GND(1'b0), ._16__Vcc(1'b1), ._15__G(1'b0),
    ._14__A4(A3), ._13__B4(n7404_2__8__4y), ._12__Y4(n74157_2__12__y4), ._11__A3(A2),
    ._10__B3(n7404_2__4__2y), ._9__Y3(n74157_2__9__y3));
  _7483 u_7483_1 (
    ._1__A4(n74157_2__12__y4), ._2__S3(n7483_1__2__s3), ._3__A3(n74157_2__9__y3), ._4__B3(n74157_3__9__y3),
    ._5__Vcc(1'b1), ._6__S2(n7483_1__6__s2), ._7__B2(n74157_3__7__y2), ._8__A2(n74157_2__7__y2),
    ._16__B4(n74157_3__12__y4), ._15__S4(n7483_1__15__s4), ._14__Cout(n7483_1__14__cout),
    ._13__Cin(n7432_2__11__4y), ._12__GND(1'b0), ._11__B1(n74157_3__4__y1), ._10__A1(n74157_2__4__y1),
    ._9__S1(n7483_1__9__s1));
  LED O3 (.in(n7483_1__15__s4));
  LED O2 (.in(n7483_1__2__s3));
  LED O0 (.in(n7483_1__9__s1));
  LED O1 (.in(n7483_1__6__s2));
  _7408 u_7408_1 (
    ._1__1A(n7404_1__12__6y), ._2__1B(n7404_1__10__5y), ._3__1Y(n7408_1__3__1y), ._4__2A(CS1), ._5__2B(CS2),
    ._6__2Y(n7408_1__6__2y), ._7__GND(1'b0), ._14__Vcc(1'b1), ._13__4B(n7404_2__2__1y),
    ._12__4A(n7404_1__10__5y), ._11__4Y(n7408_1__11__4y), ._10__3B(CS0), ._9__3A(n7408_1__6__2y),
    ._8__3Y(n7408_1__8__3y));
  _7432 u_7432_1 (
    ._1__1A(n7408_1__3__1y), ._2__1B(n7408_1__8__3y), ._3__1Y(n7432_1__3__1y), ._4__2A(n7404_1__6__3y),
    ._5__2B(n7404_2__6__3y), ._6__2Y(n7432_1__6__2y), ._7__GND(1'b0), ._14__Vcc(1'b1),
    ._13__4B(n7408_1__3__1y), ._12__4A(n7408_1__11__4y), ._11__4Y(n7432_1__11__4y),
    ._10__3B(n7404_2__10__5y), ._9__3A(n7404_1__8__4y), ._8__3Y(n7432_1__8__3y));
  _74157 u_74157_3 (
    ._1__S(n7432_1__11__4y), ._2__A1(n7432_1__3__1y), ._3__B1(n74157_1__4__y1), ._4__Y1(n74157_3__4__y1),
    ._5__A2(n7432_1__3__1y), ._6__B2(n74157_1__7__y2), ._7__Y2(n74157_3__7__y2), ._8__GND(1'b0),
    ._16__Vcc(1'b1), ._15__G(n7408_2__8__3y), ._14__A4(n7432_1__3__1y), ._13__B4(n74157_1__12__y4),
    ._12__Y4(n74157_3__12__y4), ._11__A3(n7432_1__3__1y), ._10__B3(n74157_1__9__y3), ._9__Y3(n74157_3__9__y3));
  _7486 u_7486_1 (
    ._1__1A(n7483_1__15__s4), ._2__1B(n74157_2__12__y4), ._3__1Y(n7486_1__3__1y), ._4__2A(n7486_1__3__1y),
    ._5__2B(n74157_3__12__y4), ._6__2Y(n7486_1__6__2y), ._7__GND(1'b0), ._14__Vcc(1'b1),
    ._13__4B(n7486_1__6__2y), ._12__4A(n7483_1__14__cout), ._11__4Y(n7486_1__11__4y));  // open: _10__3B, _9__3A, _8__3Y
  LED S (.in(n7483_1__15__s4));
  LED Z (.in(n7404_2__12__6y));
  LED C (.in(n7483_1__14__cout));
  LED V (.in(n7486_1__11__4y));
  _7404 u_7404_2 (
    ._1__1A(CS2), ._2__1Y(n7404_2__2__1y), ._3__2A(n7432_1__6__2y), ._4__2Y(n7404_2__4__2y), ._5__3A(A2),
    ._6__3Y(n7404_2__6__3y), ._7__GND(1'b0), ._14__Vcc(1'b1), ._13__6A(n7432_2__8__3y),
    ._12__6Y(n7404_2__12__6y), ._11__5A(A3), ._10__5Y(n7404_2__10__5y), ._9__4A(n7432_1__8__3y),
    ._8__4Y(n7404_2__8__4y));
  _7408 u_7408_2 (
    ._1__1A(B0), ._2__1B(A0), ._3__1Y(n7408_2__3__1y), ._4__2A(B1), ._5__2B(A1), ._6__2Y(n7408_2__6__2y),
    ._7__GND(1'b0), ._14__Vcc(1'b1), ._13__4B(n7404_2__2__1y), ._12__4A(CS1), ._11__4Y(n7408_2__11__4y),
    ._10__3B(n7408_1__6__2y), ._9__3A(n7404_1__10__5y), ._8__3Y(n7408_2__8__3y));
  _7432 u_7432_2 (
    ._1__1A(n7483_1__9__s1), ._2__1B(n7483_1__6__s2), ._3__1Y(n7432_2__3__1y), ._4__2A(n7432_2__3__1y),
    ._5__2B(n7483_1__2__s3), ._6__2Y(n7432_2__6__2y), ._7__GND(1'b0), ._14__Vcc(1'b1),
    ._13__4B(n7408_2__11__4y), ._12__4A(n7408_1__3__1y), ._11__4Y(n7432_2__11__4y), ._10__3B(n7432_2__6__2y),
    ._9__3A(n7483_1__15__s4), ._8__3Y(n7432_2__8__3y));

  // Notes on the sheet:
  //   S1
  //   CS2CS1
  //   CS2CS1CS0
  //   CS1'CS0'
  //   S1
  //   S2
  //   CS2'CS0'
  //   CS2CS1CS0'
  //   CS2'CS1
  //   Z
endmodule
