// Logisim project circuit_v1.circ as structural Verilog: 1 circuit, main circuit main
module main (
  input  Cs,
  input  in_2,
  input  in_3,
  input  A3,
  input  A2,
  input  A1,
  input  A0,
  input  B3,
  input  B2,
  input  B1,
  input  B0
);

  wire n7404_1__2__1y, n7404_1__4__2y, n7404_1__6__3y, n7404_2__2__1y, n7404_2__4__2y, n7404_2__6__3y,
       n7404_2__10__5y, n7404_2__12__6y, n7408_1__3__1y, n7408_1__6__2y, n7408_1__8__3y, n7408_1__11__4y,
       n7408_2__3__1y, n7408_2__6__2y, n7408_2__8__3y, n7408_2__11__4y, n7408_3__3__1y, n7408_3__6__2y,
       n7408_3__8__3y, n7408_3__11__4y, n7408_4__3__1y, n7408_4__6__2y, n7408_4__8__3y, n7408_4__11__4y,
       n7408_5__3__1y, n7408_5__6__2y, n7408_5__11__4y, n7432_1__3__1y, n7432_1__6__2y, n7432_1__8__3y,
       n7432_1__11__4y, n7432_2__3__1y, n7432_2__6__2y, n7432_2__8__3y, n7432_2__11__4y, n7432_3__3__1y,
       n7432_3__6__2y, n7432_3__8__3y, n7432_3__11__4y, n7483_1__2__s3, n7483_1__6__s2, n7483_1__14__cout,
       n7483_1__15__s4, n7483_2__14__cout, n7483_2__15__s4, n7486_1__3__1y, n74157_1__4__y1, n74157_1__7__y2,
       n74157_1__9__y3, n74157_1__12__y4;

  _7404 u_7404_1 (
    ._1__1A(in_3), ._2__1Y(n7404_1__2__1y), ._3__2A(in_2), ._4__2Y(n7404_1__4__2y), ._5__3A(Cs),
    ._6__3Y(n7404_1__6__3y), ._7__GND(1'b0), ._14__Vcc(1'b1));  // open: _13__6A, _12__6Y, _11__5A, _10__5Y, _9__4A, _8__4Y
  _7408 u_7408_1 (
    ._1__1A(Cs), ._2__1B(in_2), ._3__1Y(n7408_1__3__1y), ._4__2A(n7408_1__3__1y), ._5__2B(n7404_1__2__1y),
    ._6__2Y(n7408_1__6__2y), ._7__GND(1'b0), ._14__Vcc(1'b1), ._13__4B(n7404_1__2__1y),
    ._12__4A(n7404_1__4__2y), ._11__4Y(n7408_1__11__4y), ._10__3B(n7404_1__6__3y), ._9__3A(in_2),
    ._8__3Y(n7408_1__8__3y));
  _7404 u_7404_2 (
    ._1__1A(B0), ._2__1Y(n7404_2__2__1y), ._3__2A(B1), ._4__2Y(n7404_2__4__2y), ._5__3A(B2),
    ._6__3Y(n7404_2__6__3y), ._7__GND(1'b0), ._14__Vcc(1'b1), ._13__6A(B3), ._12__6Y(n7404_2__12__6y),
    ._11__5A(n7432_1__8__3y), ._10__5Y(n7404_2__10__5y));  // open: _9__4A, _8__4Y
  _7432 u_7432_1 (
    ._1__1A(n7408_1__11__4y), ._2__1B(n7408_1__8__3y), ._3__1Y(n7432_1__3__1y), ._4__2A(n74157_1__9__y3),
    ._5__2B(n74157_1__12__y4), ._6__2Y(n7432_1__6__2y), ._7__GND(1'b0), ._14__Vcc(1'b1),
    ._13__4B(n7432_1__6__2y), ._12__4A(n74157_1__7__y2), ._11__4Y(n7432_1__11__4y),
    ._10__3B(n7432_1__11__4y), ._9__3A(n74157_1__4__y1), ._8__3Y(n7432_1__8__3y));
  _7408 u_7408_2 (
    ._1__1A(A0), ._2__1B(B0), ._3__1Y(n7408_2__3__1y), ._4__2A(A1), ._5__2B(B1), ._6__2Y(n7408_2__6__2y),
    ._7__GND(1'b0), ._14__Vcc(1'b1), ._13__4B(A2), ._12__4A(B2), ._11__4Y(n7408_2__11__4y), ._10__3B(A3),
    ._9__3A(B3), ._8__3Y(n7408_2__8__3y));
  _7408 u_7408_3 (
    ._1__1A(n7408_1__11__4y), ._2__1B(n7404_2__2__1y), ._3__1Y(n7408_3__3__1y), ._4__2A(n7408_1__11__4y),
    ._5__2B(n7404_2__4__2y), ._6__2Y(n7408_3__6__2y), ._7__GND(1'b0), ._14__Vcc(1'b1),
    ._13__4B(n7408_1__11__4y), ._12__4A(n7404_2__6__3y), ._11__4Y(n7408_3__11__4y),
    ._10__3B(n7408_1__11__4y), ._9__3A(n7404_2__12__6y), ._8__3Y(n7408_3__8__3y));
  _7408 u_7408_4 (
    ._1__1A(n7408_5__11__4y), ._2__1B(B0), ._3__1Y(n7408_4__3__1y), ._4__2A(n7408_5__11__4y), ._5__2B(B1),
    ._6__2Y(n7408_4__6__2y), ._7__GND(1'b0), ._14__Vcc(1'b1), ._13__4B(n7408_5__11__4y), ._12__4A(B2),
    ._11__4Y(n7408_4__11__4y), ._10__3B(n7408_5__11__4y), ._9__3A(B3), ._8__3Y(n7408_4__8__3y));
  _7408 u_7408_5 (
    ._1__1A(n7408_1__3__1y), ._2__1B(in_3), ._3__1Y(n7408_5__3__1y), ._4__2A(n7404_1__2__1y),
    ._5__2B(n7404_1__6__3y), ._6__2Y(n7408_5__6__2y), ._7__GND(1'b0), ._14__Vcc(1'b1),
    ._13__4B(n7408_5__6__2y), ._12__4A(in_2), ._11__4Y(n7408_5__11__4y));  // open: _10__3B, _9__3A, _8__3Y
  _7483 u_7483_1 (
    ._1__A4(A2), ._2__S3(n7483_1__2__s3), ._3__A3(A1), ._4__B3(n7432_2__8__3y), ._5__Vcc(1'b1),
    ._6__S2(n7483_1__6__s2), ._7__B2(n7432_2__6__2y), ._8__A2(A0), ._16__B4(n7432_3__6__2y),
    ._15__S4(n7483_1__15__s4), ._14__Cout(n7483_1__14__cout), ._13__Cin(n7432_1__3__1y), ._12__GND(1'b0),
    ._11__B1(1'b0), ._10__A1(1'b1));  // open: _9__S1
  _7483 u_7483_2 (
    ._1__A4(A3), ._3__A3(1'b0), ._4__B3(1'b1), ._5__Vcc(1'b1), ._7__B2(1'b1), ._8__A2(1'b0),
    ._16__B4(n7432_3__8__3y), ._15__S4(n7483_2__15__s4), ._14__Cout(n7483_2__14__cout),
    ._13__Cin(n7483_1__14__cout), ._12__GND(1'b0), ._11__B1(1'b1), ._10__A1(1'b0));  // open: _2__S3, _6__S2, _9__S1
  _7432 u_7432_2 (
    ._1__1A(n7408_4__3__1y), ._2__1B(n7408_3__3__1y), ._3__1Y(n7432_2__3__1y), ._4__2A(n7432_2__3__1y),
    ._5__2B(n7408_5__3__1y), ._6__2Y(n7432_2__6__2y), ._7__GND(1'b0), ._14__Vcc(1'b1),
    ._13__4B(n7408_4__6__2y), ._12__4A(n7408_3__6__2y), ._11__4Y(n7432_2__11__4y), ._10__3B(n7432_2__11__4y),
    ._9__3A(n7408_5__3__1y), ._8__3Y(n7432_2__8__3y));
  _7432 u_7432_3 (
    ._1__1A(n7408_4__11__4y), ._2__1B(n7408_3__11__4y), ._3__1Y(n7432_3__3__1y), ._4__2A(n7432_3__3__1y),
    ._5__2B(n7408_5__3__1y), ._6__2Y(n7432_3__6__2y), ._7__GND(1'b0), ._14__Vcc(1'b1),
    ._13__4B(n7408_4__8__3y), ._12__4A(n7408_3__8__3y), ._11__4Y(n7432_3__11__4y), ._10__3B(n7432_3__11__4y),
    ._9__3A(n7408_5__3__1y), ._8__3Y(n7432_3__8__3y));
  LED led_1 (.in(n74157_1__9__y3));
  LED led_2 (.in(n7483_2__14__cout));
  LED led_3 (.in(n74157_1__12__y4));
  LED led_4 (.in(n74157_1__7__y2));
  LED led_5 (.in(n74157_1__4__y1));
  _74157 u_74157_1 (
    ._1__S(n7408_1__6__2y), ._2__A1(n7483_1__6__s2), ._3__B1(n7408_2__3__1y), ._4__Y1(n74157_1__4__y1),
    ._5__A2(n7483_1__2__s3), ._6__B2(n7408_2__6__2y), ._7__Y2(n74157_1__7__y2), ._8__GND(1'b0),
    ._16__Vcc(1'b1), ._15__G(1'b0), ._14__A4(n7483_2__15__s4), ._13__B4(n7408_2__8__3y),
    ._12__Y4(n74157_1__12__y4), ._11__A3(n7483_1__15__s4), ._10__B3(n7408_2__11__4y), ._9__Y3(n74157_1__9__y3));
  LED C (.in(n7483_2__14__cout));
  LED V (.in(n7486_1__3__1y));
  LED Z (.in(n7404_2__10__5y));
  _7486 u_7486_1 (
    ._1__1A(n7483_2__14__cout), ._2__1B(n7483_1__14__cout), ._3__1Y(n7486_1__3__1y), ._7__GND(1'b0),
    ._14__Vcc(1'b1));  // open: _4__2A, _5__2B, _6__2Y, _13__4B, _12__4A, _11__4Y, _10__3B, _9__3A, _8__3Y
  LED S (.in(n74157_1__9__y3));

  // Notes on the sheet:
  //   s2s1
  //   s2s1s0'
  //   s2's1
  //   s1's0'
  //   B0's1's0'
  //   B0s2's1's0
  //   s1's0'
  //   B1's1's0'
  //   B3's1's0'
  //   B1s2's1's0
  //   B3s2's1's0
  //   s2's1's0
  //   B2's1's0'
  //   B2s2's1's0
  //   s2s1s0
  //   s2s1s0
  //   s2's1'
  //   Y0
  //   Y2
  //   Y1
  //   Y3
  //   OUTPUT
endmodule
