// Logisim project circuit_v3.circ as structural Verilog: 1 circuit, main circuit main
module main (
  input  [2:0] in_1,
  input  [3:0] A,
  input  [3:0] B
);

  wire n7404_1__2__1y, n7404_1__4__2y, n7404_1__6__3y, n7404_1__8__4y, n7404_1__10__5y, n7404_1__12__6y,
       n7404_2__2__1y, n7404_2__4__2y, n7404_2__6__3y, n7404_2__8__4y, n7404_2__10__5y, n7404_2__12__6y,
       n7408_1__3__1y, n7408_1__6__2y, n7408_1__8__3y, n7408_1__11__4y, n7408_2__3__1y, n7408_2__6__2y,
       n7408_2__8__3y, n7408_2__11__4y, n7432_1__3__1y, n7432_1__6__2y, n7432_1__8__3y, n7432_1__11__4y,
       n7432_2__3__1y, n7432_2__6__2y, n7432_2__8__3y, n7432_2__11__4y, n7483_1__2__s3, n7483_1__6__s2,
       n7483_1__9__s1, n7483_1__14__cout, n7483_1__15__s4, n7486_1__3__1y, n7486_1__6__2y, n7486_1__11__4y,
       n74157_1__4__y1, n74157_1__7__y2, n74157_1__9__y3, n74157_1__12__y4, n74157_2__4__y1, n74157_2__7__y2,
       n74157_2__9__y3, n74157_2__12__y4, n74157_3__4__y1, n74157_3__7__y2, n74157_3__9__y3, n74157_3__12__y4;

  _74157 u_74157_1 (
    ._1__S(n7432_1__11__4y), ._2__A1(B[0]), ._3__B1(n7404_1__12__6y), ._4__Y1(n74157_1__4__y1),
    ._5__A2(B[1]), ._6__B2(n7404_1__10__5y), ._7__Y2(n74157_1__7__y2), ._8__GND(1'b0), ._16__Vcc(1'b1),
    ._15__G(n7408_1__6__2y), ._14__A4(B[3]), ._13__B4(n7404_2__2__1y), ._12__Y4(n74157_1__12__y4),
    ._11__A3(B[2]), ._10__B3(n7404_1__8__4y), ._9__Y3(n74157_1__9__y3));
  _7404 u_7404_1 (
    ._1__1A(in_1[0]), ._2__1Y(n7404_1__2__1y), ._3__2A(in_1[1]), ._4__2Y(n7404_1__4__2y), ._5__3A(in_1[2]),
    ._6__3Y(n7404_1__6__3y), ._7__GND(1'b0), ._14__Vcc(1'b1), ._13__6A(B[0]), ._12__6Y(n7404_1__12__6y),
    ._11__5A(B[1]), ._10__5Y(n7404_1__10__5y), ._9__4A(B[2]), ._8__4Y(n7404_1__8__4y));
  _7404 u_7404_2 (
    ._1__1A(B[3]), ._2__1Y(n7404_2__2__1y), ._3__2A(A[2]), ._4__2Y(n7404_2__4__2y), ._5__3A(n7432_1__8__3y),
    ._6__3Y(n7404_2__6__3y), ._7__GND(1'b0), ._14__Vcc(1'b1), ._13__6A(n7432_2__11__4y),
    ._12__6Y(n7404_2__12__6y), ._11__5A(A[3]), ._10__5Y(n7404_2__10__5y), ._9__4A(n7432_2__8__3y),
    ._8__4Y(n7404_2__8__4y));
  _74157 u_74157_2 (
    ._1__S(n7432_1__6__2y), ._2__A1(n7432_1__11__4y), ._3__B1(n74157_1__4__y1), ._4__Y1(n74157_2__4__y1),
    ._5__A2(n7432_1__11__4y), ._6__B2(n74157_1__7__y2), ._7__Y2(n74157_2__7__y2), ._8__GND(1'b0),
    ._16__Vcc(1'b1), ._15__G(n7408_1__6__2y), ._14__A4(n7432_1__11__4y), ._13__B4(n74157_1__12__y4),
    ._12__Y4(n74157_2__12__y4), ._11__A3(n7432_1__11__4y), ._10__B3(n74157_1__9__y3), ._9__Y3(n74157_2__9__y3));
  _7408 u_7408_1 (
    ._1__1A(in_1[2]), ._2__1B(in_1[1]), ._3__1Y(n7408_1__3__1y), ._4__2A(n7408_1__3__1y), ._5__2B(in_1[0]),
    ._6__2Y(n7408_1__6__2y), ._7__GND(1'b0), ._14__Vcc(1'b1), ._13__4B(n7408_1__3__1y),
    ._12__4A(n7404_1__2__1y), ._11__4Y(n7408_1__11__4y), ._10__3B(n7404_1__4__2y), ._9__3A(n7404_1__2__1y),
    ._8__3Y(n7408_1__8__3y));
  _7408 u_7408_2 (
    ._1__1A(n7404_1__6__3y), ._2__1B(n7404_1__2__1y), ._3__1Y(n7408_2__3__1y), ._4__2A(n7404_1__6__3y),
    ._5__2B(in_1[1]), ._6__2Y(n7408_2__6__2y), ._7__GND(1'b0), ._14__Vcc(1'b1), ._13__4B(B[0]),
    ._12__4A(A[0]), ._11__4Y(n7408_2__11__4y), ._10__3B(B[1]), ._9__3A(A[1]), ._8__3Y(n7408_2__8__3y));
  _7483 u_7483_1 (
    ._1__A4(A[3]), ._2__S3(n7483_1__2__s3), ._3__A3(A[2]), ._4__B3(n74157_2__9__y3), ._5__Vcc(1'b1),
    ._6__S2(n7483_1__6__s2), ._7__B2(n74157_2__7__y2), ._8__A2(A[1]), ._16__B4(n74157_2__12__y4),
    ._15__S4(n7483_1__15__s4), ._14__Cout(n7483_1__14__cout), ._13__Cin(n7432_1__3__1y), ._12__GND(1'b0),
    ._11__B1(n74157_2__4__y1), ._10__A1(A[0]), ._9__S1(n7483_1__9__s1));
  _7432 u_7432_1 (
    ._1__1A(n7408_1__8__3y), ._2__1B(n7408_2__6__2y), ._3__1Y(n7432_1__3__1y), ._4__2A(n7408_1__8__3y),
    ._5__2B(n7408_2__3__1y), ._6__2Y(n7432_1__6__2y), ._7__GND(1'b0), ._14__Vcc(1'b1),
    ._13__4B(n7408_1__6__2y), ._12__4A(n7408_1__8__3y), ._11__4Y(n7432_1__11__4y), ._10__3B(n7404_1__8__4y),
    ._9__3A(n7404_2__4__2y), ._8__3Y(n7432_1__8__3y));
  _74157 u_74157_3 (
    ._1__S(n7408_1__11__4y), ._2__A1(n7483_1__9__s1), ._3__B1(n7408_2__11__4y), ._4__Y1(n74157_3__4__y1),
    ._5__A2(n7483_1__6__s2), ._6__B2(n7408_2__8__3y), ._7__Y2(n74157_3__7__y2), ._8__GND(1'b0),
    ._16__Vcc(1'b1), ._15__G(1'b0), ._14__A4(n7483_1__15__s4), ._13__B4(n7404_2__8__4y),
    ._12__Y4(n74157_3__12__y4), ._11__A3(n7483_1__2__s3), ._10__B3(n7404_2__6__3y), ._9__Y3(n74157_3__9__y3));
  LED led_1 (.in(n7483_1__14__cout));
  LED led_2 (.in(n74157_3__4__y1));
  LED led_3 (.in(n74157_3__7__y2));
  LED led_4 (.in(n74157_3__12__y4));
  LED led_5 (.in(n74157_3__9__y3));
  _7432 u_7432_2 (
    ._1__1A(n74157_3__4__y1), ._2__1B(n74157_3__7__y2), ._3__1Y(n7432_2__3__1y), ._4__2A(n7432_2__3__1y),
    ._5__2B(n74157_3__9__y3), ._6__2Y(n7432_2__6__2y), ._7__GND(1'b0), ._14__Vcc(1'b1),
    ._13__4B(n7432_2__6__2y), ._12__4A(n74157_3__12__y4), ._11__4Y(n7432_2__11__4y),
    ._10__3B(n7404_2__10__5y), ._9__3A(n7404_2__2__1y), ._8__3Y(n7432_2__8__3y));
  _7486 u_7486_1 (
    ._1__1A(n74157_2__12__y4), ._2__1B(A[3]), ._3__1Y(n7486_1__3__1y), ._4__2A(n7486_1__3__1y),
    ._5__2B(n7483_1__15__s4), ._6__2Y(n7486_1__6__2y), ._7__GND(1'b0), ._14__Vcc(1'b1),
    ._13__4B(n7486_1__6__2y), ._12__4A(n7483_1__14__cout), ._11__4Y(n7486_1__11__4y));  // open: _10__3B, _9__3A, _8__3Y
  LED led_6 (.in(n7404_2__12__6y));
  LED led_7 (.in(n7483_1__14__cout));
  LED led_8 (.in(n7486_1__11__4y));
  LED led_9 (.in(n74157_3__12__y4));

  // Notes on the sheet:
  //   cs2cs1cs0
  //   cs2'cs0'
  //   cs2cs1
  //   cs1'cs0'
  //   cs2'cs1
  //   s2
  //   s1
  //   cs2cs1cs0'
  //   Output bit
  //   Z
  //   C
  //   V
  //   S
endmodule
