// Logisim project Checker.circ as structural Verilog: 3 circuits, main circuit 0_checker
module _0_checker (
  input  [8:0] Exponent,
  output isZero
);

  nor nor_1 (isZero, Exponent[0], Exponent[1], Exponent[2], Exponent[3], Exponent[4], Exponent[5], Exponent[6], Exponent[7], Exponent[8]);
endmodule

module _1_cheacker (
  input  [8:0] Exponent,
  output isOne
);

  and and_1 (isOne, Exponent[0], Exponent[1], Exponent[2], Exponent[3], Exponent[4], Exponent[5], Exponent[6], Exponent[7], Exponent[8]);
endmodule

module _32bit_0_checker (
  input  [31:0] in_1,
  output isZero
);

  nor nor_1 (isZero, in_1[0], in_1[1], in_1[2], in_1[3], in_1[4], in_1[5], in_1[6], in_1[7], in_1[8], in_1[9], in_1[10], in_1[11], in_1[12], in_1[13], in_1[14], in_1[15], in_1[16], in_1[17], in_1[18], in_1[19], in_1[20], in_1[21], in_1[22], in_1[23], in_1[24], in_1[25], in_1[26], in_1[27], in_1[28], in_1[29], in_1[30], in_1[31]);

  // Notes on the sheet:
  //   Input
endmodule
