// Logisim project Flag.circ as structural Verilog: 1 circuit, main circuit Flag Finder
module Flag_Finder (
  input  Result__0,
  input  Underflow,
  input  Overflow,
  input  [31:0] Significand,
  input  [8:0] Exponent,
  output Denormalized,
  output Underflow_2,
  output Overflow_2,
  output NaN,
  output INF
);

  wire and_1_out, n0_checker_1_iszero, n1_cheacker_1_isone, n32bit_0_checker_1_iszero, not_1_out, not_2_out,
       not_3_out, not_4_out;

  _32bit_0_checker u_32bit_0_checker_1 (.in_1(Significand), .isZero(n32bit_0_checker_1_iszero));
  _0_checker u_0_checker_1 (.Exponent(Exponent), .isZero(n0_checker_1_iszero));
  _1_cheacker u_1_cheacker_1 (.Exponent(Exponent), .isOne(n1_cheacker_1_isone));
  not not_1 (not_1_out, n32bit_0_checker_1_iszero);
  not not_2 (not_2_out, Result__0);
  not not_3 (not_3_out, Underflow);
  and and_1 (and_1_out, not_3_out, not_4_out);
  not not_4 (not_4_out, Overflow);
  and and_2 (NaN, not_1_out, and_1_out, n1_cheacker_1_isone);
  and and_3 (INF, n32bit_0_checker_1_iszero, and_1_out, n1_cheacker_1_isone);
  and and_4 (Denormalized, not_2_out, n0_checker_1_iszero, and_1_out);

  assign Overflow_2 = Overflow;
  assign Underflow_2 = Underflow;
endmodule
