// Logisim project IPH.circ as structural Verilog: 5 circuits, main circuit Input Processing Handler
module Input_Processing_Handler (
  input  [31:0] A,
  input  [31:0] B,
  output [31:0] L_significant,
  output [31:0] S_significant,
  output [8:0] Ea_nEb,
  output [8:0] LARGE_EXP,
  output LARGE_SIGN,
  output SMALL_SIGN
);

  wire comparator_1_eq, exp_process_1_ea_eb, exp_process_1_larger_s_sign, exp_process_1_smaller_s_sign,
       input_process_1_sign_bit, input_process_2_sign_bit;
  wire [8:0] input_process_1_exponential, input_process_2_exponential;
  wire [31:0] input_process_1_output_number, input_process_2_output_number, multiplexer_1_out,
       multiplexer_2_out, rightshifter_1_output;

  Input_process input_process_1 (
    .exponential(input_process_1_exponential), .\input (A), .output_number(input_process_1_output_number),
    .sign_bit(input_process_1_sign_bit));
  Input_process input_process_2 (
    .exponential(input_process_2_exponential), .\input (B), .output_number(input_process_2_output_number),
    .sign_bit(input_process_2_sign_bit));
  Exp_process exp_process_1 (
    .Ea(input_process_1_exponential), .Eb(input_process_2_exponential), .Sa(input_process_1_sign_bit),
    .Sb(input_process_2_sign_bit), .Smaller_s_sign(exp_process_1_smaller_s_sign),
    .Ea_Eb(exp_process_1_ea_eb), .Ea_nEb(Ea_nEb), .Large_exp(LARGE_EXP),
    .Larger_s_sign(exp_process_1_larger_s_sign));
  Multiplexer #(.width(32)) multiplexer_1 (
    .in0(input_process_2_output_number), .in1(input_process_1_output_number), .out(multiplexer_1_out),
    .sel(exp_process_1_ea_eb), .en(1'b1));
  Multiplexer #(.width(32)) multiplexer_2 (
    .in0(input_process_1_output_number), .in1(input_process_2_output_number), .out(multiplexer_2_out),
    .sel(exp_process_1_ea_eb), .en(1'b1));
  Comparator #(.width(9)) comparator_1 (.a(Ea_nEb), .b({9{1'b0}}), .eq(comparator_1_eq));  // open: gt, lt
  Sign_choose sign_choose_1 (
    .L_Sig(multiplexer_1_out), .L_Sign(exp_process_1_larger_s_sign), .S_sign(exp_process_1_smaller_s_sign),
    .S_Sig(rightshifter_1_output), .Ea_nEb_0(comparator_1_eq), .L_Sign_2(LARGE_SIGN), .S_Sign_2(SMALL_SIGN));
  rightShifter rightshifter_1 (.\input (multiplexer_2_out), .\output (rightshifter_1_output), .shifting_amount(Ea_nEb));
  sig_choose sig_choose_1 (
    .L_Sig(multiplexer_1_out), .S_Sig(rightshifter_1_output), .Ea_nEb_0(comparator_1_eq),
    .L_Sig_2(L_significant), .S_Sig_2(S_significant));
endmodule

// ExpP
module Exp_process (
  input  [8:0] Ea,
  input  [8:0] Eb,
  input  Sa,
  input  Sb,
  output Ea_Eb,
  output [8:0] Ea_nEb,
  output [8:0] Large_exp,
  output Larger_s_sign,
  output Smaller_s_sign
);

  wire [8:0] multiplexer_2_out;

  Comparator #(.width(9), .mode("unsigned")) comparator_1 (.a(Ea), .b(Eb), .gt(Ea_Eb));  // open: eq, lt
  Multiplexer #(.width(9)) multiplexer_1 (.in0(Eb), .in1(Ea), .out(Large_exp), .sel(Ea_Eb), .en(1'b1));
  Multiplexer #(.width(9)) multiplexer_2 (.in0(Ea), .in1(Eb), .out(multiplexer_2_out), .sel(Ea_Eb), .en(1'b1));
  Multiplexer multiplexer_3 (.in0(Sb), .in1(Sa), .out(Larger_s_sign), .sel(Ea_Eb), .en(1'b1));
  Multiplexer multiplexer_4 (.in0(Sa), .in1(Sb), .out(Smaller_s_sign), .sel(Ea_Eb), .en(1'b1));
  Subtractor #(.width(9)) subtractor_1 (.a(Large_exp), .b(multiplexer_2_out), .out(Ea_nEb));  // open: bin, bout
endmodule

// IP
module Input_process (
  input  [31:0] \input ,
  output [31:0] output_number,
  output [8:0] exponential,
  output sign_bit
);

  wire or_1_out;

  Multiplexer #(.width(32)) multiplexer_1 (
    .in0({32{1'b0}}), .in1({1'b1, \input [21:0], {9{1'b0}}}), .out(output_number), .sel(or_1_out), .en(1'b1));
  or or_1 (or_1_out, \input [0], \input [1], \input [2], \input [3], \input [4], \input [5], \input [6], \input [7], \input [8], \input [9], \input [10], \input [11], \input [12], \input [13], \input [14], \input [15], \input [16], \input [17], \input [18], \input [19], \input [20], \input [21], \input [22], \input [23], \input [24], \input [25], \input [26], \input [27], \input [28], \input [29], \input [30]);

  assign exponential = \input [30:22];
  assign sign_bit = \input [31];
endmodule

module sig_choose (
  input  [31:0] L_Sig,
  input  [31:0] S_Sig,
  input  Ea_nEb_0,
  output [31:0] L_Sig_2,
  output [31:0] S_Sig_2
);

  wire comparator_1_eq, comparator_1_gt, or_1_out;
  wire [31:0] multiplexer_1_out, multiplexer_3_out;

  Comparator #(.width(32), .mode("unsigned")) comparator_1 (
    .a(L_Sig), .b(S_Sig), .gt(comparator_1_gt), .eq(comparator_1_eq));  // open: lt
  Multiplexer #(.width(32), .enable("false")) multiplexer_1 (
    .in0(S_Sig), .in1(L_Sig), .out(multiplexer_1_out), .sel(or_1_out));
  or or_1 (or_1_out, comparator_1_gt, comparator_1_eq);
  Multiplexer #(.width(32), .enable("false")) multiplexer_2 (
    .in0(L_Sig), .in1(multiplexer_1_out), .out(L_Sig_2), .sel(Ea_nEb_0));
  Multiplexer #(.width(32), .enable("false")) multiplexer_3 (
    .in0(L_Sig), .in1(S_Sig), .out(multiplexer_3_out), .sel(or_1_out));
  Multiplexer #(.width(32), .enable("false")) multiplexer_4 (
    .in0(S_Sig), .in1(multiplexer_3_out), .out(S_Sig_2), .sel(Ea_nEb_0));
endmodule

module Sign_choose (
  input  [31:0] L_Sig,
  input  L_Sign,
  input  S_sign,
  input  [31:0] S_Sig,
  input  Ea_nEb_0,
  output L_Sign_2,
  output S_Sign_2
);

  wire comparator_1_eq, comparator_1_gt, multiplexer_1_out, multiplexer_3_out, or_1_out;

  Comparator #(.width(32), .mode("unsigned")) comparator_1 (
    .a(L_Sig), .b(S_Sig), .gt(comparator_1_gt), .eq(comparator_1_eq));  // open: lt
  Multiplexer #(.enable("false")) multiplexer_1 (.in0(S_sign), .in1(L_Sign), .out(multiplexer_1_out), .sel(or_1_out));
  or or_1 (or_1_out, comparator_1_gt, comparator_1_eq);
  Multiplexer #(.enable("false")) multiplexer_2 (.in0(L_Sign), .in1(multiplexer_1_out), .out(L_Sign_2), .sel(Ea_nEb_0));
  Multiplexer #(.enable("false")) multiplexer_3 (.in0(L_Sign), .in1(S_sign), .out(multiplexer_3_out), .sel(or_1_out));
  Multiplexer #(.enable("false")) multiplexer_4 (.in0(S_sign), .in1(multiplexer_3_out), .out(S_Sign_2), .sel(Ea_nEb_0));
endmodule
