// Logisim project Output.circ as structural Verilog: 1 circuit, main circuit Output
module Output (
  input  [31:0] Significand,
  input  [8:0] Exponent,
  input  Sign,
  output [31:0] out_4
);


  assign out_4 = {Sign, Exponent, Significand[31:10]};
endmodule
