// Logisim project RoundedNormalizer.circ as structural Verilog: 1 circuit, main circuit Rounded Normalizer
module Rounded_Normalizer (
  input  Carry,
  input  [8:0] Exponent,
  input  Overflow,
  input  Underflow,
  output [8:0] changed_Exponent,
  output overflow_2
);

  wire adder_1_cout, not_1_out, or_1_out;

  Adder #(.width(9)) adder_1 (.a(Exponent), .b({9{1'b0}}), .out(changed_Exponent), .cin(Carry), .cout(adder_1_cout));
  or or_1 (or_1_out, adder_1_cout, Overflow);
  not not_1 (not_1_out, Underflow);
  and and_1 (overflow_2, or_1_out, not_1_out);
endmodule
