// Logisim project Rounder.circ as structural Verilog: 1 circuit, main circuit Rounder
module Rounder (
  input  [31:0] significand,
  output [31:0] rounded_significand,
  output Cout
);

  wire or_1_out, or_2_out;
  wire [10:10] and_1_out;

  or or_1 (or_1_out, significand[0], significand[1], significand[2], significand[4], significand[5], significand[6], significand[7]);
  or or_2 (or_2_out, or_1_out, significand[8], significand[10]);
  and and_1 (and_1_out[10], or_2_out, significand[9]);
  Adder #(.width(32)) adder_1 (
    .a({{21{1'b0}}, and_1_out[10], {10{1'b0}}}), .b({significand[31:10], {10{1'b0}}}),
    .out(rounded_significand), .cin(1'b0), .cout(Cout));

  // Notes on the sheet:
  //   Cout=1(Denormalized)
endmodule
