// Logisim project Significand Adder.circ as structural Verilog: 1 circuit, main circuit Significand Adder
module Significand_Adder (
  input  [31:0] L_Sig,
  input  [31:0] S_Sig,
  input  L_Sign,
  input  S_Sign,
  output [31:0] Result,
  output Carry_Out,
  output Result___0,
  output Sign_Bit
);

  wire or_1_out, or_2_out, xor_1_out;

  xor xor_1 (xor_1_out, L_Sign, S_Sign);
  ALU alu_1 (.A(L_Sig), .B(S_Sig), ._0_add__1_sub(xor_1_out), .Result(Result), .Carry_Out(Carry_Out));
  Multiplexer #(.enable("false")) multiplexer_1 (.in0(1'b0), .in1(L_Sign), .out(Sign_Bit), .sel(or_2_out));
  or or_1 (or_1_out, Result[16], Carry_Out);
  or or_2 (or_2_out, Result[0], Result[1], Result[2], Result[3], Result[4], Result[5], Result[6], Result[7], Result[8], Result[9], Result[10], Result[11], Result[12], Result[13], Result[14], Result[15], Result[17], Result[18], Result[19], Result[20], Result[21], Result[22], Result[23], Result[24], Result[25], Result[26], Result[27], Result[28], Result[29], Result[30], Result[31], or_1_out);
  not not_1 (Result___0, or_2_out);
endmodule
