// Logisim project Branch_Detection.circ as structural Verilog: 1 circuit, main circuit BranchDetection
module BranchDetection (
  input  zero,
  input  branch_eq,
  input  branch_op,
  output Branch_taken
);

  wire xnor_1_out;

  xnor xnor_1 (xnor_1_out, zero, branch_eq);
  and and_1 (Branch_taken, xnor_1_out, branch_op);
endmodule
