// Logisim project Instruction_Decode.circ as structural Verilog: 1 circuit, main circuit Instruction Decode
module Instruction_Decode (
  input  [19:0] in_1,
  output [3:0] SftAmt,
  output [3:0] Rd,
  output [3:0] Rt,
  output [3:0] Rs,
  output [3:0] OpCode,
  output [7:0] Immidiate,
  output [7:0] Jump_Address
);


  assign Immidiate = in_1[7:0];
  assign Jump_Address = in_1[15:8];
  assign OpCode = in_1[19:16];
  assign Rd = in_1[7:4];
  assign Rs = in_1[15:12];
  assign Rt = in_1[11:8];
  assign SftAmt = in_1[3:0];
endmodule
