// Logisim project Load hazard detect.circ as structural Verilog: 1 circuit, main circuit main
module main (
  input  ID_EX_memRead,
  input  ID_EX_Rt___Rs,
  input  ID_EX_Rt___Rt,
  input  ID_EX_Rt___0,
  output Hazard_detection
);

  wire and_1_out, and_2_out, and_3_out, not_1_out;

  not not_1 (not_1_out, ID_EX_Rt___0);
  and and_1 (and_1_out, ID_EX_memRead, ID_EX_Rt___Rs, not_1_out);
  and and_2 (and_2_out, ID_EX_memRead, ID_EX_Rt___Rs, not_1_out);
  and and_3 (and_3_out, ID_EX_memRead, ID_EX_Rt___Rt, not_1_out);
  or or_1 (Hazard_detection, and_1_out, and_2_out, and_3_out);
endmodule
