// Logisim project Load-Store Forwarding.circ as structural Verilog: 1 circuit, main circuit main
module main (
  input  MEM_WB_memRead,
  input  EX_MEM_MemWrite,
  input  EX_MEM_Rt___MEM_WB_WR,
  output forwardA
);

  and and_1 (forwardA, MEM_WB_memRead, EX_MEM_MemWrite, EX_MEM_Rt___MEM_WB_WR);
endmodule
