// Logisim project MIPS_with_pipeline.circ as structural Verilog: 1 circuit, main circuit main
module main (
  input  start,
  input  Clear_All,
  output [7:0] sp,
  output [7:0] t4,
  output [7:0] t3,
  output [7:0] t2,
  output [7:0] t1,
  output [7:0] t0,
  output [7:0] zero
);

  wire alu_8_by_art_1_p4, and_1_out, and_2_out, and_3_out, and_4_out, and_5_out, and_6_out, and_7_out,
       and_8_out, and_9_out, and_10_out, and_11_out, and_12_out, Branch_Detection_Unit_branch_taken,
       clock_1_out, comparator_1_eq, comparator_2_eq, comparator_3_eq, comparator_4_eq, comparator_5_eq,
       comparator_6_eq, comparator_7_eq, comparator_8_eq, comparator_9_eq, comparator_10_eq,
       Data_Hazard_hazard_detection, EX_MEM_branching_eq_2, EX_MEM_branching_op_2, EX_MEM_memtoreg_2,
       EX_MEM_mr_2, EX_MEM_mw_2, EX_MEM_rw_2, EX_MEM_zero_2, ID_EX_alusrc_2, ID_EX_branching_eq_2,
       ID_EX_branching_op_2, ID_EX_memtoreg_2, ID_EX_mr_2, ID_EX_mw_2, ID_EX_regdst_2, ID_EX_rw_2,
       ID_EX_shift_2, Load_Store_Fwd_forwarda, main_1_alu_src, main_1_brancing_op, main_1_brncing_eql,
       main_1_j, main_1_mem_read, main_1_mem_to_reg, main_1_mem_write, main_1_reg_dst, main_1_reg_write,
       main_1_shift, MEM_WB_memread_2, MEM_WB_memtoreg_2, MEM_WB_rw_2, not_1_out, not_2_out, not_3_out,
       not_4_out, or_1_out, or_2_out, RAAAW_Forwarding_forwarda, RAAAW_Forwarding_forwardb;
  wire [1:0] forwarding_unit_1_forwarda, forwarding_unit_1_forwardb;
  wire [2:0] ALU_control_unit_alu_opcode, ID_EX_aluop_2;
  wire [3:0] EX_MEM_rt_2, EX_MEM_wr_2, ID_EX_rd_2, ID_EX_rs_2, ID_EX_rt_2, Instruction_Decode_opcode,
       Instruction_Decode_rd, Instruction_Decode_rs, Instruction_Decode_rt, Instruction_Decode_sftamt,
       MEM_WB_wr_2, multiplexer_9_out;
  wire [7:0] adder_1_out, adder_2_out, alu_8_by_art_1_p5, bit_extender_1_out, EX_MEM_alu_2,
       EX_MEM_immidiate_2, EX_MEM_pc_2, EX_MEM_reg_rt_data_2, ID_EX_immidiate_2, ID_EX_pc_2,
       ID_EX_readdata1_2, ID_EX_readdata2_2, ID_EX_shiftamt_2, if_id_1_pc_2, Instruction_Decode_immidiate,
       Instruction_Decode_jump_address, MEM_WB_alu_2, MEM_WB_memdata_2, multiplexer_1_out, multiplexer_2_out,
       multiplexer_3_out, multiplexer_6_out, multiplexer_7_out, multiplexer_8_out, multiplexer_10_out,
       multiplexer_11_out, multiplexer_12_out, multiplexer_13_out, multiplexer_14_out, multiplexer_15_out,
       multiplexer_16_out, ram_1_data, register_1_q, register_2_read_data_1, register_2_read_data_2;
  wire [19:0] EX_MEM_instruction_2, ID_EX_instruction_2, if_id_1_output, MEM_WB_instruction_2,
       multiplexer_4_out, multiplexer_5_out, rom_1_data;

  not not_1 (not_1_out, Data_Hazard_hazard_detection);
  Multiplexer #(.width(8), .enable("false")) multiplexer_1 (
    .in0(multiplexer_2_out), .in1({8{1'b0}}), .out(multiplexer_1_out), .sel(start));
  Multiplexer #(.width(8), .enable("false")) multiplexer_2 (
    .in0(multiplexer_3_out), .in1(adder_2_out), .out(multiplexer_2_out),
    .sel(Branch_Detection_Unit_branch_taken));
  Register register_1 (.D(multiplexer_1_out), .en(not_1_out), .Q(register_1_q), .clk(clock_1_out), .clr(Clear_All));
  Clock clock_1 (.out(clock_1_out));
  Multiplexer #(.width(8), .enable("false")) multiplexer_3 (
    .in0(adder_1_out), .in1(Instruction_Decode_jump_address), .out(multiplexer_3_out), .sel(main_1_j));
  Adder adder_1 (.a(8'h1), .b(register_1_q), .out(adder_1_out));  // open: cin, cout
  // Probe on multiplexer_5_out
  ROM #(.dataWidth(20)) rom_1 (.addr(register_1_q), .data(rom_1_data), .sel(1'b1));
  Multiplexer #(.width(20), .enable("false")) multiplexer_4 (
    .in0(rom_1_data), .in1(if_id_1_output), .out(multiplexer_4_out), .sel(Data_Hazard_hazard_detection));
  Comparator #(.width(4)) comparator_1 (
    .a(Instruction_Decode_rs), .b(MEM_WB_wr_2), .eq(comparator_1_eq));  // open: gt, lt
  Comparator #(.width(4)) comparator_2 (
    .a(Instruction_Decode_rt), .b(MEM_WB_wr_2), .eq(comparator_2_eq));  // open: gt, lt
  or or_1 (or_1_out, Branch_Detection_Unit_branch_taken, main_1_j);
  not not_2 (not_2_out, or_1_out);
  Multiplexer #(.width(20), .enable("false")) multiplexer_5 (
    .in0(20'he0000), .in1(multiplexer_4_out), .out(multiplexer_5_out), .sel(not_2_out));
  IF_ID if_id_1 (
    .PC(multiplexer_6_out), .Data(multiplexer_5_out), .Enable(clock_1_out), .CLK(clock_1_out),
    .Clear(Clear_All), .PC_2(if_id_1_pc_2), .Output(if_id_1_output));
  Multiplexer #(.width(8), .enable("false")) multiplexer_6 (
    .in0(adder_1_out), .in1(if_id_1_pc_2), .out(multiplexer_6_out), .sel(Data_Hazard_hazard_detection));
  RAAAW_Forwarding RAAAW_Forwarding (
    .MEM_WB_WR___IF_ID_Rs(comparator_1_eq), .MEM_WB_RW(MEM_WB_rw_2), .MEM_WB_WR___IF_ID_Rt(comparator_2_eq),
    .ForwardA(RAAAW_Forwarding_forwarda), .ForwardB(RAAAW_Forwarding_forwardb));
  // Probe on if_id_1_output
  Instruction_Decode Instruction_Decode (
    .in_1(if_id_1_output), .SftAmt(Instruction_Decode_sftamt), .Rd(Instruction_Decode_rd),
    .Rt(Instruction_Decode_rt), .Rs(Instruction_Decode_rs), .OpCode(Instruction_Decode_opcode),
    .Immidiate(Instruction_Decode_immidiate), .Jump_Address(Instruction_Decode_jump_address));
  assign bit_extender_1_out = {{4{Instruction_Decode_sftamt[3]}}, Instruction_Decode_sftamt};  // Bit_Extender bit_extender_1
  control_main main_1 (
    .Opcode(Instruction_Decode_opcode), .J(main_1_j), .Reg_Write(main_1_reg_write),
    .Mem_Read(main_1_mem_read), .Mem_Write(main_1_mem_write), .Mem_to_Reg(main_1_mem_to_reg),
    .Brancing_Op(main_1_brancing_op), .Reg_Dst(main_1_reg_dst), .ALU_Src(main_1_alu_src),
    .Brncing_eql(main_1_brncing_eql), .shift(main_1_shift));
  Register register_2 (
    .Write_Data(multiplexer_16_out), .Write_Register(MEM_WB_wr_2), .Read_Register_1(Instruction_Decode_rs),
    .Read_Register_2(Instruction_Decode_rt), .CLK(clock_1_out), .Clear(Clear_All), .Reg_Write(MEM_WB_rw_2),
    .Zero(zero), .t0(t0), .t1(t1), .Read_Data_1(register_2_read_data_1), .t2(t2), .t3(t3), .t4(t4), .sp(sp),
    .Read_Data_2(register_2_read_data_2));  // open: ra
  Comparator #(.width(4)) comparator_3 (
    .a(Instruction_Decode_rs), .b(ID_EX_rt_2), .eq(comparator_3_eq));  // open: gt, lt
  Comparator #(.width(4)) comparator_4 (
    .a(Instruction_Decode_rt), .b(ID_EX_rt_2), .eq(comparator_4_eq));  // open: gt, lt
  Comparator #(.width(4)) comparator_5 (.a(ID_EX_rt_2), .b(4'b0000), .eq(comparator_5_eq));  // open: gt, lt
  OP_CODE_ALU_main ALU_control_unit (.opcode(Instruction_Decode_opcode), .alu_opcode(ALU_control_unit_alu_opcode));
  Multiplexer #(.width(8), .enable("false")) multiplexer_7 (
    .in0(register_2_read_data_1), .in1(multiplexer_16_out), .out(multiplexer_7_out),
    .sel(RAAAW_Forwarding_forwarda));
  Load_hazard_detect_main Data_Hazard (
    .ID_EX_memRead(ID_EX_mr_2), .ID_EX_Rt___Rs(comparator_3_eq), .ID_EX_Rt___Rt(comparator_4_eq),
    .ID_EX_Rt___0(comparator_5_eq), .Hazard_detection(Data_Hazard_hazard_detection));
  Multiplexer #(.width(8), .enable("false")) multiplexer_8 (
    .in0(register_2_read_data_2), .in1(multiplexer_16_out), .out(multiplexer_8_out),
    .sel(RAAAW_Forwarding_forwardb));
  or or_2 (or_2_out, Data_Hazard_hazard_detection, Branch_Detection_Unit_branch_taken);
  not not_3 (not_3_out, or_2_out);
  and and_1 (and_1_out, not_3_out, main_1_brancing_op);
  and and_2 (and_2_out, not_3_out, main_1_brncing_eql);
  and and_3 (and_3_out, not_3_out, main_1_mem_read);
  and and_4 (and_4_out, not_3_out, main_1_mem_write);
  and and_5 (and_5_out, not_3_out, main_1_reg_write);
  and and_6 (and_6_out, not_3_out, main_1_alu_src);
  and and_7 (and_7_out, not_3_out, main_1_reg_dst);
  and and_8 (and_8_out, not_3_out, main_1_mem_to_reg);
  and and_9 (and_9_out, not_3_out, main_1_shift);
  ID_EX ID_EX (
    .PC(if_id_1_pc_2), .Branching_op(and_1_out), .Branching_eq(and_2_out), .Instruction(if_id_1_output),
    .Rs(Instruction_Decode_rs), .Rd(Instruction_Decode_rd), .Rt(Instruction_Decode_rt), .MR(and_3_out),
    .MW(and_4_out), .RW(and_5_out), .ALUOP(ALU_control_unit_alu_opcode), .ShiftAmt(bit_extender_1_out),
    .immidiate(Instruction_Decode_immidiate), .ALUSrc(and_6_out), .RegDst(and_7_out), .MemtoReg(and_8_out),
    .shift(and_9_out), .ReadData1(multiplexer_7_out), .ReadData2(multiplexer_8_out), .Enable(clock_1_out),
    .CLK(clock_1_out), .Clear(Clear_All), .PC_2(ID_EX_pc_2), .Branching_op_2(ID_EX_branching_op_2),
    .Branching_eq_2(ID_EX_branching_eq_2), .Instruction_2(ID_EX_instruction_2), .Rs_2(ID_EX_rs_2),
    .Rd_2(ID_EX_rd_2), .Rt_2(ID_EX_rt_2), .MR_2(ID_EX_mr_2), .MW_2(ID_EX_mw_2), .RW_2(ID_EX_rw_2),
    .ALUOP_2(ID_EX_aluop_2), .ShiftAmt_2(ID_EX_shiftamt_2), .immidiate_2(ID_EX_immidiate_2),
    .ALUSrc_2(ID_EX_alusrc_2), .RegDst_2(ID_EX_regdst_2), .MemtoReg_2(ID_EX_memtoreg_2),
    .shift_2(ID_EX_shift_2), .ReadData1_2(ID_EX_readdata1_2), .ReadData2_2(ID_EX_readdata2_2));
  // Probe on ID_EX_instruction_2
  Multiplexer #(.width(4), .enable("false")) multiplexer_9 (
    .in0(ID_EX_rt_2), .in1(ID_EX_rd_2), .out(multiplexer_9_out), .sel(ID_EX_regdst_2));
  Comparator #(.width(4)) comparator_6 (.a(ID_EX_rs_2), .b(EX_MEM_wr_2), .eq(comparator_6_eq));  // open: gt, lt
  Comparator #(.width(4)) comparator_7 (.a(ID_EX_rt_2), .b(EX_MEM_wr_2), .eq(comparator_7_eq));  // open: gt, lt
  Comparator #(.width(4)) comparator_8 (.a(ID_EX_rs_2), .b(MEM_WB_wr_2), .eq(comparator_8_eq));  // open: gt, lt
  Comparator #(.width(4)) comparator_9 (.a(ID_EX_rt_2), .b(MEM_WB_wr_2), .eq(comparator_9_eq));  // open: gt, lt
  Multiplexer #(.select(2), .width(8), .enable("false")) multiplexer_10 (
    .in0(ID_EX_readdata1_2), .in1(multiplexer_16_out), .in2(EX_MEM_alu_2), .out(multiplexer_10_out),
    .sel(forwarding_unit_1_forwarda));  // open: in3
  Multiplexer #(.width(8), .enable("false")) multiplexer_11 (
    .in0(multiplexer_12_out), .in1(ID_EX_immidiate_2), .out(multiplexer_11_out), .sel(ID_EX_alusrc_2));
  Multiplexer #(.select(2), .width(8), .enable("false")) multiplexer_12 (
    .in0(ID_EX_readdata2_2), .in1(multiplexer_16_out), .in2(EX_MEM_alu_2), .out(multiplexer_12_out),
    .sel(forwarding_unit_1_forwardb));  // open: in3
  Multiplexer #(.width(8), .enable("false")) multiplexer_13 (
    .in0(multiplexer_11_out), .in1(multiplexer_10_out), .out(multiplexer_13_out), .sel(ID_EX_shift_2));
  Forwarding_Unit forwarding_unit_1 (
    .EX_MEM_Rd___ID_EX_Rs(comparator_6_eq), .EX_MEM_Rd___ID_EX_Rt(comparator_7_eq),
    .MEM_WB_Rd___ID_EX_Rs(comparator_8_eq), .MEM_WB_Rd___ID_EX_Rt(comparator_9_eq),
    .EX_MEM_regWrite(EX_MEM_rw_2), .MEM_WB_regWrite(MEM_WB_rw_2), .ForwardA(forwarding_unit_1_forwarda),
    .ForwardB(forwarding_unit_1_forwardb));
  Multiplexer #(.width(8), .enable("false")) multiplexer_14 (
    .in0(multiplexer_10_out), .in1(ID_EX_shiftamt_2), .out(multiplexer_14_out), .sel(ID_EX_shift_2));
  // ALU_8_by_ART alu_8_by_art_1: pin names not known; wires that end beside it: multiplexer_14_out, multiplexer_13_out, ID_EX_aluop_2, alu_8_by_art_1_p4, alu_8_by_art_1_p5
  not not_4 (not_4_out, Branch_Detection_Unit_branch_taken);
  and and_10 (and_10_out, not_4_out, ID_EX_rw_2);
  and and_11 (and_11_out, not_4_out, ID_EX_mw_2);
  and and_12 (and_12_out, not_4_out, ID_EX_mr_2);
  EX_MEM EX_MEM (
    .PC(ID_EX_pc_2), .ALU(alu_8_by_art_1_p5), .WR(multiplexer_9_out), .RW(and_10_out), .MW(and_11_out),
    .MR(and_12_out), .Reg_rt_data(multiplexer_12_out), .Branching_op(ID_EX_branching_op_2),
    .Branching_eq(ID_EX_branching_eq_2), .Immidiate(ID_EX_immidiate_2), .MemtoReg(ID_EX_memtoreg_2),
    .zero(alu_8_by_art_1_p4), .Rt(ID_EX_rt_2), .Instruction(ID_EX_instruction_2), .Enable(clock_1_out),
    .CLK(clock_1_out), .Clear(Clear_All), .PC_2(EX_MEM_pc_2), .ALU_2(EX_MEM_alu_2), .WR_2(EX_MEM_wr_2),
    .RW_2(EX_MEM_rw_2), .MW_2(EX_MEM_mw_2), .MR_2(EX_MEM_mr_2), .Reg_rt_data_2(EX_MEM_reg_rt_data_2),
    .Branching_op_2(EX_MEM_branching_op_2), .Branching_eq_2(EX_MEM_branching_eq_2),
    .Immidiate_2(EX_MEM_immidiate_2), .MemtoReg_2(EX_MEM_memtoreg_2), .zero_2(EX_MEM_zero_2),
    .Rt_2(EX_MEM_rt_2), .Instruction_2(EX_MEM_instruction_2));
  Adder adder_2 (.a(EX_MEM_immidiate_2), .b(EX_MEM_pc_2), .out(adder_2_out));  // open: cin, cout
  BranchDetection Branch_Detection_Unit (
    .zero(EX_MEM_zero_2), .branch_eq(EX_MEM_branching_eq_2), .branch_op(EX_MEM_branching_op_2),
    .Branch_taken(Branch_Detection_Unit_branch_taken));
  Load_Store_Forwarding_main Load_Store_Fwd (
    .MEM_WB_memRead(MEM_WB_memread_2), .EX_MEM_MemWrite(EX_MEM_mw_2),
    .EX_MEM_Rt___MEM_WB_WR(comparator_10_eq), .forwardA(Load_Store_Fwd_forwarda));
  Comparator #(.width(4)) comparator_10 (.a(EX_MEM_rt_2), .b(MEM_WB_wr_2), .eq(comparator_10_eq));  // open: gt, lt
  Multiplexer #(.width(8), .enable("false")) multiplexer_15 (
    .in0(EX_MEM_reg_rt_data_2), .in1(MEM_WB_memdata_2), .out(multiplexer_15_out),
    .sel(Load_Store_Fwd_forwarda));
  // Probe on EX_MEM_instruction_2
  RAM #(.bus("separate")) ram_1 (
    .addr(EX_MEM_alu_2), .din(multiplexer_15_out), .data(ram_1_data), .str(EX_MEM_mw_2), .sel(1'b1),
    .clk(clock_1_out), .ld(EX_MEM_mr_2), .clr(Clear_All));
  MEM_WB MEM_WB (
    .ALU(EX_MEM_alu_2), .RW(EX_MEM_rw_2), .WR(EX_MEM_wr_2), .MemData(ram_1_data),
    .MemtoReg(EX_MEM_memtoreg_2), .MemRead(EX_MEM_mr_2), .Instruction(EX_MEM_instruction_2),
    .Enable(clock_1_out), .CLK(clock_1_out), .Clear(Clear_All), .ALU_2(MEM_WB_alu_2), .RW_2(MEM_WB_rw_2),
    .WR_2(MEM_WB_wr_2), .MemData_2(MEM_WB_memdata_2), .MemtoReg_2(MEM_WB_memtoreg_2),
    .MemRead_2(MEM_WB_memread_2), .Instruction_2(MEM_WB_instruction_2));
  // Probe on MEM_WB_instruction_2
  Multiplexer #(.width(8), .enable("false")) multiplexer_16 (
    .in0(MEM_WB_alu_2), .in1(MEM_WB_memdata_2), .out(multiplexer_16_out), .sel(MEM_WB_memtoreg_2));

  // Notes on the sheet:
  //   Data Hazard, disable
  //   Branch
  //   Jump
  //   PC + 1
  //   contents of rom_1 (hex, n*v repeats v):
  //   b0104 b0204 11100 11200 1300 3400 4*e0000
  //   Instruction Rewrite
  //   Branch, NOP
  //   PC Rewrite
  //   Control unit
  //   Register file
  //   Data Hazard| Branch, Reset
  //   RegDst
  //   Forwarding
  //   Forwarding
  //   Shifting
  //   ALU Src
  //   Shifting
  //   Branch, Reset
  //   PC+1+ branch target
  //   MemtoReg
endmodule
