// Logisim project MIPS_without_pipeline.circ as structural Verilog: 1 circuit, main circuit MIPS
module MIPS (
  input  start,
  input  in_2,
  input  Clear_All,
  output [7:0] sp,
  output [7:0] t4,
  output [7:0] t3,
  output [7:0] t2,
  output [7:0] t1,
  output [7:0] t0,
  output [7:0] zero
);

  wire alu_8_by_art_1_p4, Branch_Detection_branch_taken, clock_1_out, Control_Unit_alu_src,
       Control_Unit_brancing_op, Control_Unit_brncing_eql, Control_Unit_j, Control_Unit_mem_read,
       Control_Unit_mem_to_reg, Control_Unit_mem_write, Control_Unit_reg_dst, Control_Unit_reg_write,
       Control_Unit_shift;
  wire [2:0] ALU_opcode_alu_opcode;
  wire [3:0] Instruction_Decode_opcode, Instruction_Decode_rd, Instruction_Decode_rs, Instruction_Decode_rt,
       Instruction_Decode_sftamt, multiplexer_4_out;
  wire [7:0] adder_1_out, adder_2_out, alu_8_by_art_1_p5, bit_extender_1_out, Instruction_Decode_immidiate,
       Instruction_Decode_jump_address, multiplexer_1_out, multiplexer_2_out, multiplexer_3_out,
       multiplexer_5_out, multiplexer_6_out, multiplexer_7_out, multiplexer_8_out, ram_1_data,
       RegFile_read_data_1, RegFile_read_data_2, register_1_q;
  wire [19:0] rom_1_data;

  Multiplexer #(.width(8), .enable("false")) multiplexer_1 (
    .in0(multiplexer_3_out), .in1(Instruction_Decode_jump_address), .out(multiplexer_1_out),
    .sel(Control_Unit_j));
  Multiplexer #(.width(8), .enable("false")) multiplexer_2 (
    .in0(multiplexer_1_out), .in1({8{1'b0}}), .out(multiplexer_2_out), .sel(start));
  Clock clock_1 (.out(clock_1_out));
  Register register_1 (.D(multiplexer_2_out), .en(in_2), .Q(register_1_q), .clk(clock_1_out), .clr(Clear_All));
  Instruction_Decode Instruction_Decode (
    .in_1(rom_1_data), .SftAmt(Instruction_Decode_sftamt), .Rd(Instruction_Decode_rd),
    .Rt(Instruction_Decode_rt), .Rs(Instruction_Decode_rs), .OpCode(Instruction_Decode_opcode),
    .Immidiate(Instruction_Decode_immidiate), .Jump_Address(Instruction_Decode_jump_address));
  ROM #(.dataWidth(20)) rom_1 (.addr(register_1_q), .data(rom_1_data), .sel(1'b1));
  Multiplexer #(.width(8), .enable("false")) multiplexer_3 (
    .in0(adder_1_out), .in1(adder_2_out), .out(multiplexer_3_out), .sel(Branch_Detection_branch_taken));
  Adder adder_1 (.a(8'h1), .b(register_1_q), .out(adder_1_out));  // open: cin, cout
  Adder adder_2 (.a(adder_1_out), .b(Instruction_Decode_immidiate), .out(adder_2_out));  // open: cin, cout
  assign bit_extender_1_out = {{4{Instruction_Decode_sftamt[3]}}, Instruction_Decode_sftamt};  // Bit_Extender bit_extender_1
  Multiplexer #(.width(4), .enable("false")) multiplexer_4 (
    .in0(Instruction_Decode_rt), .in1(Instruction_Decode_rd), .out(multiplexer_4_out),
    .sel(Control_Unit_reg_dst));
  control_main Control_Unit (
    .Opcode(Instruction_Decode_opcode), .J(Control_Unit_j), .Reg_Write(Control_Unit_reg_write),
    .Mem_Read(Control_Unit_mem_read), .Mem_Write(Control_Unit_mem_write),
    .Mem_to_Reg(Control_Unit_mem_to_reg), .Brancing_Op(Control_Unit_brancing_op),
    .Reg_Dst(Control_Unit_reg_dst), .ALU_Src(Control_Unit_alu_src), .Brncing_eql(Control_Unit_brncing_eql),
    .shift(Control_Unit_shift));
  Register RegFile (
    .Write_Data(multiplexer_8_out), .Write_Register(multiplexer_4_out),
    .Read_Register_1(Instruction_Decode_rs), .Read_Register_2(Instruction_Decode_rt), .CLK(clock_1_out),
    .Clear(Clear_All), .Reg_Write(Control_Unit_reg_write), .Zero(zero), .t0(t0), .t1(t1),
    .Read_Data_1(RegFile_read_data_1), .t2(t2), .t3(t3), .t4(t4), .sp(sp), .Read_Data_2(RegFile_read_data_2));  // open: ra
  Multiplexer #(.width(8), .enable("false")) multiplexer_5 (
    .in0(RegFile_read_data_2), .in1(Instruction_Decode_immidiate), .out(multiplexer_5_out),
    .sel(Control_Unit_alu_src));
  OP_CODE_ALU_main ALU_opcode (.opcode(Instruction_Decode_opcode), .alu_opcode(ALU_opcode_alu_opcode));
  Multiplexer #(.width(8), .enable("false")) multiplexer_6 (
    .in0(multiplexer_5_out), .in1(RegFile_read_data_1), .out(multiplexer_6_out), .sel(Control_Unit_shift));
  BranchDetection Branch_Detection (
    .zero(alu_8_by_art_1_p4), .branch_eq(Control_Unit_brncing_eql), .branch_op(Control_Unit_brancing_op),
    .Branch_taken(Branch_Detection_branch_taken));
  Multiplexer #(.width(8), .enable("false")) multiplexer_7 (
    .in0(RegFile_read_data_1), .in1(bit_extender_1_out), .out(multiplexer_7_out), .sel(Control_Unit_shift));
  // ALU_8_by_ART alu_8_by_art_1: pin names not known; wires that end beside it: multiplexer_7_out, multiplexer_6_out, ALU_opcode_alu_opcode, alu_8_by_art_1_p4, alu_8_by_art_1_p5
  Multiplexer #(.width(8), .enable("false")) multiplexer_8 (
    .in0(alu_8_by_art_1_p5), .in1(ram_1_data), .out(multiplexer_8_out), .sel(Control_Unit_mem_to_reg));
  RAM #(.bus("separate")) ram_1 (
    .addr(alu_8_by_art_1_p5), .din(RegFile_read_data_2), .data(ram_1_data), .str(Control_Unit_mem_write),
    .sel(1'b1), .clk(clock_1_out), .ld(Control_Unit_mem_read), .clr(Clear_All));

  // Notes on the sheet:
  //   Jump
  //   contents of rom_1 (hex, n*v repeats v):
  //   35119 35214 41230 41240 41250 f0000 16100 4*e0000
  //   Branch
  //   RegDst
  //   ALUSrc
  //   ShiftB
  //   ShiftA
  //   MemtoReg
endmodule
