// Logisim project OP_CODE_ALU.circ as structural Verilog: 1 circuit, main circuit main
module main (
  input  [3:0] opcode,
  output [2:0] alu_opcode
);

  ROM #(.addrWidth(4), .dataWidth(3)) rom_1 (.addr(opcode), .data(alu_opcode), .sel(1'b1));

  // Notes on the sheet:
  //   contents of rom_1 (hex, n*v repeats v):
  //   0 0 1 2 0 4 3 6 5 1 3 0 2 1 1
endmodule
