// Logisim project PC.circ as structural Verilog: 1 circuit, main circuit PC
module PC (
  input  [7:0] PC,
  input  RegWrite,
  input  CLK,
  output [7:0] out_4,
  output [19:0] Instruction
);

  Register u_PC (.en(RegWrite), .Q(out_4), .clk(CLK));  // open: D, clr
  ROM #(.dataWidth(20)) rom_1 (.addr(out_4), .data(Instruction));  // open: sel
endmodule
