// Logisim project Pipe_reg.circ as structural Verilog: 4 circuits, main circuit IF|ID
module IF_ID (
  input  [7:0] PC,
  input  [19:0] Data,
  input  Enable,
  input  CLK,
  input  Clear,
  output [7:0] PC_2,
  output [19:0] Output
);

  Register register_1 (.D(PC), .en(Enable), .Q(PC_2), .clk(CLK), .clr(Clear));
  Register #(.width(20)) register_2 (.D(Data), .en(Enable), .Q(Output), .clk(CLK), .clr(Clear));
endmodule

module ID_EX (
  input  [7:0] PC,
  input  Branching_op,
  input  Branching_eq,
  input  [19:0] Instruction,
  input  [3:0] Rs,
  input  [3:0] Rd,
  input  [3:0] Rt,
  input  MR,
  input  MW,
  input  RW,
  input  [2:0] ALUOP,
  input  [7:0] ShiftAmt,
  input  [7:0] immidiate,
  input  ALUSrc,
  input  RegDst,
  input  MemtoReg,
  input  shift,
  input  [7:0] ReadData1,
  input  [7:0] ReadData2,
  input  Enable,
  input  CLK,
  input  Clear,
  output [7:0] PC_2,
  output Branching_op_2,
  output Branching_eq_2,
  output [19:0] Instruction_2,
  output [3:0] Rs_2,
  output [3:0] Rd_2,
  output [3:0] Rt_2,
  output MR_2,
  output MW_2,
  output RW_2,
  output [2:0] ALUOP_2,
  output [7:0] ShiftAmt_2,
  output [7:0] immidiate_2,
  output ALUSrc_2,
  output RegDst_2,
  output MemtoReg_2,
  output shift_2,
  output [7:0] ReadData1_2,
  output [7:0] ReadData2_2
);

  Register register_1 (.D(PC), .en(Enable), .Q(PC_2), .clk(CLK), .clr(Clear));
  Register #(.width(1)) register_2 (.D(Branching_op), .en(Enable), .Q(Branching_op_2), .clk(CLK), .clr(Clear));
  Register #(.width(1)) register_3 (.D(Branching_eq), .en(Enable), .Q(Branching_eq_2), .clk(CLK), .clr(Clear));
  Register #(.width(20)) u_Instruction (.D(Instruction), .en(Enable), .Q(Instruction_2), .clk(CLK), .clr(Clear));
  Register #(.width(4)) register_4 (.D(Rs), .en(Enable), .Q(Rs_2), .clk(CLK), .clr(Clear));
  Register #(.width(4)) register_5 (.D(Rd), .en(Enable), .Q(Rd_2), .clk(CLK), .clr(Clear));
  Register #(.width(4)) register_6 (.D(Rt), .en(Enable), .Q(Rt_2), .clk(CLK), .clr(Clear));
  Register #(.width(1)) register_7 (.D(MR), .en(Enable), .Q(MR_2), .clk(CLK), .clr(Clear));
  Register #(.width(1)) register_8 (.D(MW), .en(Enable), .Q(MW_2), .clk(CLK), .clr(Clear));
  Register #(.width(1)) u_RW (.D(RW), .en(Enable), .Q(RW_2), .clk(CLK), .clr(Clear));
  Register #(.width(3)) register_9 (.D(ALUOP), .en(Enable), .Q(ALUOP_2), .clk(CLK), .clr(Clear));
  Register register_10 (.D(ShiftAmt), .en(Enable), .Q(ShiftAmt_2), .clk(CLK), .clr(Clear));
  Register register_11 (.D(immidiate), .en(Enable), .Q(immidiate_2), .clk(CLK), .clr(Clear));
  Register #(.width(1)) register_12 (.D(ALUSrc), .en(Enable), .Q(ALUSrc_2), .clk(CLK), .clr(Clear));
  Register #(.width(1)) register_13 (.D(RegDst), .en(Enable), .Q(RegDst_2), .clk(CLK), .clr(Clear));
  Register #(.width(1)) register_14 (.D(MemtoReg), .en(Enable), .Q(MemtoReg_2), .clk(CLK), .clr(Clear));
  Register #(.width(1)) register_15 (.D(shift), .en(Enable), .Q(shift_2), .clk(CLK), .clr(Clear));
  Register register_16 (.D(ReadData1), .en(Enable), .Q(ReadData1_2), .clk(CLK), .clr(Clear));
  Register register_17 (.D(ReadData2), .en(Enable), .Q(ReadData2_2), .clk(CLK), .clr(Clear));
endmodule

module EX_MEM (
  input  [7:0] PC,
  input  [7:0] ALU,
  input  [3:0] WR,
  input  RW,
  input  MW,
  input  MR,
  input  [7:0] Reg_rt_data,
  input  Branching_op,
  input  Branching_eq,
  input  [7:0] Immidiate,
  input  MemtoReg,
  input  zero,
  input  [3:0] Rt,
  input  [19:0] Instruction,
  input  Enable,
  input  CLK,
  input  Clear,
  output [7:0] PC_2,
  output [7:0] ALU_2,
  output [3:0] WR_2,
  output RW_2,
  output MW_2,
  output MR_2,
  output [7:0] Reg_rt_data_2,
  output Branching_op_2,
  output Branching_eq_2,
  output [7:0] Immidiate_2,
  output MemtoReg_2,
  output zero_2,
  output [3:0] Rt_2,
  output [19:0] Instruction_2
);

  Register register_1 (.D(PC), .en(Enable), .Q(PC_2), .clk(CLK), .clr(Clear));
  Register register_2 (.D(ALU), .en(Enable), .Q(ALU_2), .clk(CLK), .clr(Clear));
  Register #(.width(4)) register_3 (.D(WR), .en(Enable), .Q(WR_2), .clk(CLK), .clr(Clear));
  Register #(.width(1)) register_4 (.D(RW), .en(Enable), .Q(RW_2), .clk(CLK), .clr(Clear));
  Register #(.width(1)) register_5 (.D(MW), .en(Enable), .Q(MW_2), .clk(CLK), .clr(Clear));
  Register #(.width(1)) register_6 (.D(MR), .en(Enable), .Q(MR_2), .clk(CLK), .clr(Clear));
  Register register_7 (.D(Reg_rt_data), .en(Enable), .Q(Reg_rt_data_2), .clk(CLK), .clr(Clear));
  Register #(.width(1)) register_8 (.D(Branching_op), .en(Enable), .Q(Branching_op_2), .clk(CLK), .clr(Clear));
  Register #(.width(1)) register_9 (.D(Branching_eq), .en(Enable), .Q(Branching_eq_2), .clk(CLK), .clr(Clear));
  Register register_10 (.D(Immidiate), .en(Enable), .Q(Immidiate_2), .clk(CLK), .clr(Clear));
  Register #(.width(1)) register_11 (.D(MemtoReg), .en(Enable), .Q(MemtoReg_2), .clk(CLK), .clr(Clear));
  Register #(.width(1)) register_12 (.D(zero), .en(Enable), .Q(zero_2), .clk(CLK), .clr(Clear));
  Register #(.width(4)) register_13 (.D(Rt), .en(Enable), .Q(Rt_2), .clk(CLK), .clr(Clear));
  Register #(.width(20)) u_Instruction (.D(Instruction), .en(Enable), .Q(Instruction_2), .clk(CLK), .clr(Clear));
endmodule

module MEM_WB (
  input  [7:0] ALU,
  input  RW,
  input  [3:0] WR,
  input  [7:0] MemData,
  input  MemtoReg,
  input  MemRead,
  input  [19:0] Instruction,
  input  Enable,
  input  CLK,
  input  Clear,
  output [7:0] ALU_2,
  output RW_2,
  output [3:0] WR_2,
  output [7:0] MemData_2,
  output MemtoReg_2,
  output MemRead_2,
  output [19:0] Instruction_2
);

  Register register_1 (.D(ALU), .en(Enable), .Q(ALU_2), .clk(CLK), .clr(Clear));
  Register #(.width(1)) register_2 (.D(RW), .en(Enable), .Q(RW_2), .clk(CLK), .clr(Clear));
  Register #(.width(4)) register_3 (.D(WR), .en(Enable), .Q(WR_2), .clk(CLK), .clr(Clear));
  Register register_4 (.D(MemData), .en(Enable), .Q(MemData_2), .clk(CLK), .clr(Clear));
  Register #(.width(1)) register_5 (.D(MemtoReg), .en(Enable), .Q(MemtoReg_2), .clk(CLK), .clr(Clear));
  Register #(.width(1)) register_6 (.D(MemRead), .en(Enable), .Q(MemRead_2), .clk(CLK), .clr(Clear));
  Register #(.width(20)) u_Instruction (.D(Instruction), .en(Enable), .Q(Instruction_2), .clk(CLK), .clr(Clear));
endmodule
