// Logisim project RAAAW_forwarding.circ as structural Verilog: 1 circuit, main circuit RAAAW Forwarding
module RAAAW_Forwarding (
  input  MEM_WB_WR___IF_ID_Rs,
  input  MEM_WB_RW,
  input  MEM_WB_WR___IF_ID_Rt,
  output ForwardA,
  output ForwardB
);

  and and_1 (ForwardA, MEM_WB_WR___IF_ID_Rs, MEM_WB_RW);
  and and_2 (ForwardB, MEM_WB_RW, MEM_WB_WR___IF_ID_Rt);
endmodule
