// Logisim project Register_file_1.circ as structural Verilog: 1 circuit, main circuit Registers
module Registers (
  input  [3:0] READ_REGISTER_1,
  input  [3:0] READ_REGISTER_2,
  input  [3:0] WRITE_REGISTER,
  input  [7:0] WRITE_DATA,
  input  CLK,
  input  REG_WRITE,
  input  CLEAR,
  output [7:0] ZERO,
  output [7:0] t0,
  output [7:0] t1,
  output [7:0] READ_DATA_1,
  output [7:0] t2,
  output [7:0] t3,
  output [7:0] t4,
  output [7:0] sp,
  output [7:0] ra,
  output [7:0] READ_DATA_2
);

  wire demultiplexer_1_out0, demultiplexer_1_out1, demultiplexer_1_out2, demultiplexer_1_out3,
       demultiplexer_1_out4, demultiplexer_1_out5, demultiplexer_1_out6, demultiplexer_1_out7;

  Demultiplexer #(.select(4), .disabled(0)) demultiplexer_1 (
    .out0(demultiplexer_1_out0), .out1(demultiplexer_1_out1), .out2(demultiplexer_1_out2),
    .out3(demultiplexer_1_out3), .out4(demultiplexer_1_out4), .out5(demultiplexer_1_out5),
    .out6(demultiplexer_1_out6), .out7(demultiplexer_1_out7), .in(1'b1), .sel(WRITE_REGISTER), .en(REG_WRITE));  // open: out8, out9, out10, out11, out12, out13, out14, out15
  Register u_ZERO (.D(WRITE_DATA), .en(demultiplexer_1_out0), .Q(ZERO), .clk(CLK));  // open: clr
  Register u_t0 (.D(WRITE_DATA), .en(demultiplexer_1_out1), .Q(t0), .clk(CLK));  // open: clr
  Register u_t1 (.D(WRITE_DATA), .en(demultiplexer_1_out2), .Q(t1), .clk(CLK), .clr(CLEAR));
  Register u_t2 (.D(WRITE_DATA), .en(demultiplexer_1_out3), .Q(t2), .clk(CLK), .clr(CLEAR));
  Register u_t3 (.D(WRITE_DATA), .en(demultiplexer_1_out4), .Q(t3), .clk(CLK), .clr(CLEAR));
  Register u_t4 (.D(WRITE_DATA), .en(demultiplexer_1_out5), .Q(t4), .clr(CLEAR));  // open: clk
  Register u_SP (.D(WRITE_DATA), .en(demultiplexer_1_out6), .Q(sp), .clk(CLK), .clr(CLEAR));
  Register u_ra (.D(WRITE_DATA), .en(demultiplexer_1_out7), .Q(ra), .clk(CLK), .clr(CLEAR));
  Multiplexer #(.select(4), .width(8), .enable("false")) multiplexer_1 (
    .in0(ZERO), .in1(t0), .in2(t1), .in3(t2), .in4(t3), .in5(t4), .in6(sp), .in7(ra), .out(READ_DATA_1),
    .sel(READ_REGISTER_1));  // open: in8, in9, in10, in11, in12, in13, in14, in15
  Multiplexer #(.select(4), .width(8), .enable("false")) multiplexer_2 (
    .in0(ZERO), .in1(t0), .in2(t1), .in3(t2), .in4(t3), .in5(t4), .in6(sp), .in7(ra), .out(READ_DATA_2),
    .sel(READ_REGISTER_2));  // open: in8, in9, in10, in11, in12, in13, in14, in15
endmodule
