// Logisim project Register_file_2.circ as structural Verilog: 1 circuit, main circuit Register
module Register (
  input  [7:0] Write_Data,
  input  [3:0] Write_Register,
  input  [3:0] Read_Register_1,
  input  [3:0] Read_Register_2,
  input  Reg_Write,
  input  CLK,
  input  Clear,
  output [7:0] Zero,
  output [7:0] t0,
  output [7:0] t1,
  output [7:0] Read_Data_1,
  output [7:0] t2,
  output [7:0] t3,
  output [7:0] t4,
  output [7:0] sp,
  output [7:0] ra,
  output [7:0] Read_Data_2
);

  wire demultiplexer_1_out0, demultiplexer_1_out1, demultiplexer_1_out2, demultiplexer_1_out3,
       demultiplexer_1_out4, demultiplexer_1_out5, demultiplexer_1_out6, demultiplexer_1_out7, or_1_out;
  wire [7:0] multiplexer_1_out;

  Demultiplexer #(.select(4), .disabled(0)) demultiplexer_1 (
    .out0(demultiplexer_1_out0), .out1(demultiplexer_1_out1), .out2(demultiplexer_1_out2),
    .out3(demultiplexer_1_out3), .out4(demultiplexer_1_out4), .out5(demultiplexer_1_out5),
    .out6(demultiplexer_1_out6), .out7(demultiplexer_1_out7), .in(1'b1), .sel(Write_Register), .en(Reg_Write));  // open: out8, out9, out10, out11, out12, out13, out14, out15
  Multiplexer #(.width(8), .enable("false")) multiplexer_1 (
    .in0(Write_Data), .in1({8{1'b1}}), .out(multiplexer_1_out), .sel(Clear));
  or or_1 (or_1_out, demultiplexer_1_out6, Clear);
  Register_part u_Zero (.D(Write_Data), .en(demultiplexer_1_out0), .Q(Zero), .clk(CLK), .clr(Clear));
  Register_part u_t0 (.D(Write_Data), .en(demultiplexer_1_out1), .Q(t0), .clk(CLK), .clr(Clear));
  Register_part u_t1 (.D(Write_Data), .en(demultiplexer_1_out2), .Q(t1), .clk(CLK), .clr(Clear));
  Register_part u_t2 (.D(Write_Data), .en(demultiplexer_1_out3), .Q(t2), .clk(CLK), .clr(Clear));
  Register_part u_t3 (.D(Write_Data), .en(demultiplexer_1_out4), .Q(t3), .clk(CLK), .clr(Clear));
  Register_part u_t4 (.D(Write_Data), .en(demultiplexer_1_out5), .Q(t4), .clk(CLK), .clr(Clear));
  Register_part u_sp (.D(multiplexer_1_out), .en(or_1_out), .Q(sp), .clk(CLK));  // open: clr
  Register_part u_ra (.D(Write_Data), .en(demultiplexer_1_out7), .Q(ra), .clk(CLK), .clr(Clear));
  Multiplexer #(.select(4), .width(8), .enable("false")) multiplexer_2 (
    .in0(Zero), .in1(t0), .in2(t1), .in3(t2), .in4(t3), .in5(t4), .in6(sp), .in7(ra), .out(Read_Data_1),
    .sel(Read_Register_1));  // open: in8, in9, in10, in11, in12, in13, in14, in15
  Multiplexer #(.select(4), .width(8), .enable("false")) multiplexer_3 (
    .in0(Zero), .in1(t0), .in2(t1), .in3(t2), .in4(t3), .in5(t4), .in6(sp), .in7(ra), .out(Read_Data_2),
    .sel(Read_Register_2));  // open: in8, in9, in10, in11, in12, in13, in14, in15
endmodule
