// Logisim project control.circ as structural Verilog: 1 circuit, main circuit main
module main (
  input  [3:0] Opcode,
  output J,
  output Reg_Write,
  output Mem_Read,
  output Mem_Write,
  output Mem_to_Reg,
  output Brancing_Op,
  output Reg_Dst,
  output ALU_Src,
  output Brncing_eql,
  output shift
);

  ROM #(.addrWidth(4), .dataWidth(10)) rom_1 (
    .addr(Opcode),
    .data({J, Reg_Write, Mem_Read, Mem_Write, Mem_to_Reg, Brancing_Op, Reg_Dst, ALU_Src, Brncing_eql, shift}),
    .sel(1'b1));

  // Notes on the sheet:
  //   contents of rom_1 (hex, n*v repeats v):
  //   1a4 44 104 104 108 108 104 109 109 108 108 104 108 12 10 200
endmodule
