// Logisim project control_previous.circ as structural Verilog: 1 circuit, main circuit main
module main (
  input  [3:0] Opcode,
  output J,
  output Reg_Write,
  output Mem_Read,
  output Mem_Write,
  output Mem_to_Reg,
  output Brancing_Op,
  output Reg_Dst,
  output ALU_Src,
  output Brncing_eql,
  output shift
);

  wire and_2_out, and_3_out, and_4_out, and_5_out, and_9_out, and_10_out, and_11_out, and_12_out, and_13_out,
       and_14_out, and_15_out, and_16_out, and_17_out, and_19_out, and_20_out, not_1_out, not_2_out,
       not_3_out, not_4_out, not_5_out, not_6_out, not_7_out, not_8_out, not_9_out, not_10_out, not_11_out,
       not_12_out, not_13_out, not_14_out, not_15_out, not_16_out, not_17_out, not_18_out, not_19_out,
       not_20_out, not_21_out, not_22_out, not_23_out, not_24_out, not_25_out, not_26_out, not_27_out,
       not_28_out, not_29_out, not_30_out, not_31_out, not_32_out, not_33_out, not_34_out, not_35_out;

  and and_1 (J, Opcode[3], Opcode[2], Opcode[1], Opcode[0]);
  not not_1 (not_1_out, Opcode[1]);
  not not_2 (not_2_out, Opcode[0]);
  not not_3 (not_3_out, Opcode[3]);
  not not_4 (not_4_out, Opcode[3]);
  not not_5 (not_5_out, Opcode[2]);
  not not_6 (not_6_out, Opcode[3]);
  not not_7 (not_7_out, Opcode[2]);
  not not_8 (not_8_out, Opcode[1]);
  not not_9 (not_9_out, Opcode[0]);
  not not_10 (not_10_out, Opcode[3]);
  not not_11 (not_11_out, Opcode[2]);
  not not_12 (not_12_out, Opcode[1]);
  not not_13 (not_13_out, Opcode[3]);
  not not_14 (not_14_out, Opcode[2]);
  not not_15 (not_15_out, Opcode[1]);
  not not_16 (not_16_out, Opcode[0]);
  not not_17 (not_17_out, Opcode[1]);
  not not_18 (not_18_out, Opcode[0]);
  not not_19 (not_19_out, Opcode[1]);
  not not_20 (not_20_out, Opcode[0]);
  not not_21 (not_21_out, Opcode[3]);
  not not_22 (not_22_out, Opcode[2]);
  not not_23 (not_23_out, Opcode[1]);
  not not_24 (not_24_out, Opcode[2]);
  not not_25 (not_25_out, Opcode[0]);
  not not_26 (not_26_out, Opcode[3]);
  not not_27 (not_27_out, Opcode[2]);
  not not_28 (not_28_out, Opcode[3]);
  not not_29 (not_29_out, Opcode[0]);
  not not_30 (not_30_out, Opcode[2]);
  not not_31 (not_31_out, Opcode[1]);
  not not_32 (not_32_out, Opcode[3]);
  not not_33 (not_33_out, Opcode[2]);
  not not_34 (not_34_out, Opcode[1]);
  not not_35 (not_35_out, Opcode[0]);
  and and_2 (and_2_out, not_1_out, not_2_out);
  and and_3 (and_3_out, not_3_out, Opcode[1]);
  and and_4 (and_4_out, not_4_out, Opcode[2]);
  and and_5 (and_5_out, Opcode[3], not_5_out);
  and and_6 (Mem_Read, not_6_out, not_7_out, not_8_out, not_9_out);
  and and_7 (Mem_Write, not_10_out, not_11_out, not_12_out, Opcode[0]);
  and and_8 (Mem_to_Reg, not_13_out, not_14_out, not_15_out, not_16_out);
  and and_9 (and_9_out, Opcode[3], Opcode[2], not_17_out, Opcode[0]);
  and and_10 (and_10_out, Opcode[3], Opcode[2], Opcode[1], not_18_out);
  and and_11 (and_11_out, Opcode[2], not_19_out, not_20_out);
  and and_12 (and_12_out, not_21_out, Opcode[2], Opcode[0]);
  and and_13 (and_13_out, Opcode[3], not_22_out, not_23_out);
  and and_14 (and_14_out, Opcode[3], not_24_out, not_25_out);
  and and_15 (and_15_out, not_26_out, not_27_out);
  and and_16 (and_16_out, not_28_out, Opcode[1], not_29_out);
  and and_17 (and_17_out, not_30_out, Opcode[1], Opcode[0]);
  and and_18 (Brncing_eql, Opcode[3], Opcode[2], not_31_out, Opcode[0]);
  and and_19 (and_19_out, not_32_out, Opcode[2], Opcode[1], Opcode[0]);
  and and_20 (and_20_out, Opcode[3], not_33_out, not_34_out, not_35_out);
  or or_1 (Reg_Write, and_2_out, and_3_out, and_4_out, and_5_out);
  or or_2 (Brancing_Op, and_9_out, and_10_out);
  or or_3 (Reg_Dst, and_11_out, and_12_out, and_13_out, and_14_out);
  or or_4 (ALU_Src, and_15_out, and_16_out, and_17_out);
  or or_5 (shift, and_19_out, and_20_out);
endmodule
