// Logisim project ex_forwarding_unit.circ as structural Verilog: 1 circuit, main circuit Forwarding Unit
module Forwarding_Unit (
  input  EX_MEM_Rd___ID_EX_Rs,
  input  EX_MEM_Rd___ID_EX_Rt,
  input  MEM_WB_Rd___ID_EX_Rs,
  input  MEM_WB_Rd___ID_EX_Rt,
  input  EX_MEM_regWrite,
  input  MEM_WB_regWrite,
  output [1:0] ForwardA,
  output [1:0] ForwardB
);

  wire and_1_out, and_2_out, and_3_out, and_4_out, and_5_out, not_1_out, not_2_out, not_3_out;

  not not_1 (not_1_out, EX_MEM_Rd___ID_EX_Rs);
  not not_2 (not_2_out, EX_MEM_Rd___ID_EX_Rt);
  not not_3 (not_3_out, EX_MEM_regWrite);
  and and_1 (and_1_out, MEM_WB_Rd___ID_EX_Rt, MEM_WB_regWrite);
  and and_2 (and_2_out, not_1_out, MEM_WB_Rd___ID_EX_Rs, MEM_WB_regWrite);
  and and_3 (and_3_out, MEM_WB_Rd___ID_EX_Rs, MEM_WB_regWrite, not_3_out);
  and and_4 (and_4_out, not_2_out, and_1_out);
  and and_5 (and_5_out, and_1_out, not_3_out);
  and and_6 (ForwardA[1], EX_MEM_Rd___ID_EX_Rs, EX_MEM_regWrite);
  or or_1 (ForwardA[0], and_2_out, and_3_out);
  and and_7 (ForwardB[1], EX_MEM_Rd___ID_EX_Rt, EX_MEM_regWrite);
  or or_2 (ForwardB[0], and_4_out, and_5_out);
endmodule
